// Logisim project ejemplo06-03-20.circ as structural Verilog
module \not  (
  input  X,
  output minus_X
);

  Transistor transistor_1 (.in(1'b1), .out(minus_X), .gate(X));
  Transistor #(.\type ("n")) transistor_2 (.in(1'b0), .out(minus_X), .gate(X));
endmodule

module implicacion (
  input  X,
  input  Y,
  output minus_X_v_Y
);

  wire not_1_minus_x;

  \not  not_1 (.X(X), .minus_X(not_1_minus_x));
  or or_1 (minus_X_v_Y, not_1_minus_x, Y);
endmodule

module ejemplo (
  input  X,
  input  Y,
  input  Z,
  output out_4
);

  wire not_1_out, not_2_out, not_3_out, or_1_out, or_2_out, or_3_out;

  not not_1 (not_1_out, X);
  not not_2 (not_2_out, Y);
  not not_3 (not_3_out, Z);
  or or_1 (or_1_out, X, Y);
  or or_2 (or_2_out, not_1_out, Z);
  or or_3 (or_3_out, not_2_out, Z);
  and3 and3_1 (.X(or_1_out), .Y(or_2_out), .Z(or_3_out), .out_4(out_4));
endmodule

module and3 (
  input  X,
  input  Y,
  input  Z,
  output out_4
);

  wire and_1_out;

  and and_1 (and_1_out, X, Y);
  and and_2 (out_4, and_1_out, Z);
endmodule

module triagular (
  input  E2,
  input  E1,
  input  E0,
  output triagular
);

  wire and_1_out, and_2_out, and_3_out, and_4_out, and_5_out, not_1_out, not_2_out, not_3_out;

  not not_1 (not_1_out, E2);
  not not_2 (not_2_out, E1);
  not not_3 (not_3_out, E0);
  and and_1 (and_1_out, not_1_out, E0);
  and and_2 (and_2_out, not_1_out, not_2_out, E0);
  and and_3 (and_3_out, E2, E1, not_3_out);
  and and_4 (and_4_out, not_1_out, E1, E0);
  and and_5 (and_5_out, E2, E1, not_3_out);
  or or_1 (triagular, and_5_out, and_4_out, and_2_out);
  or or_2 (triagular, and_3_out, and_1_out);
endmodule
